# Fritzing sketch esp8266_chirp (saved by Fritzing 0.9.3b)
breadboards: 1

parts:
  U1 = NodeMCU V1.0
  Chirp!_Soil_Moisture_Sensor1 = Chirp! Soil Moisture Sensor v2.7.3

nets:
  N1: U1.D0, U1.RST
  N2: U1.D1, Chirp!_Soil_Moisture_Sensor1.pin_2
  N3: U1.D2, Chirp!_Soil_Moisture_Sensor1.pin_3
  N4: U1.3V3, Chirp!_Soil_Moisture_Sensor1.Pin_1
  N5: U1.GND, Chirp!_Soil_Moisture_Sensor1.pin_5

notes:
  Connection of HW reset for deep sleep
  I2C bus

custom parts:
  NodeMCU V1.0: ESP8266 based NodeMCU
